// Logisim project KeyboardInterface.circ as structural Verilog
module InitialResponse (
  input  PS2ClockIn,
  input  PS2DataIn,
  output PS2ClockOut,
  output PS2DataOut,
  output PS2ClockPullDown,
  output PS2DataPullDown
);

  wire not_1_out, not_2_out, ResetKeyboard_q;

  not not_1 (not_1_out, PS2ClockIn);
  T_Flip_Flop ResetKeyboard (.T(PS2ClockPullDown), .clk(not_2_out), .Q(ResetKeyboard_q));  // open: Qn, reset, preset
  not not_2 (not_2_out, PS2ClockPullDown);
  and and_1 (PS2ClockPullDown, ResetKeyboard_q, not_1_out);
  not not_3 (PS2ClockOut, not_1_out);

  assign PS2DataOut = PS2DataIn;
  assign PS2DataPullDown = 1'b0;
endmodule
